// Logisim project PROJECT.circ as structural Verilog: 1 circuit, main circuit main
module main (
  input  Sign__Bit_7__MSB,
  input  Bit_6,
  input  Bit_5,
  input  Bit_4,
  input  Bit_3,
  input  Bit_2,
  input  Bit_1,
  input  Bit_0_LSB,
  output out_9,
  output out_10,
  output out_11,
  output out_12,
  output out_13,
  output out_14,
  output out_15,
  output out_16
);


  assign out_9 = Sign__Bit_7__MSB;
  assign out_10 = Bit_6;
  assign out_11 = Bit_5;
  assign out_12 = Bit_4;
  assign out_13 = Bit_3;
  assign out_14 = Bit_2;
  assign out_15 = Bit_1;
  assign out_16 = Bit_0_LSB;
endmodule
